# Fritzing sketch System (saved by Fritzing 0.9.3b)
breadboards: 1

parts:
  Part1 = HX711 Weighing Sensor Module
  Part2 = Arduino Nano (Rev3.0)
  Part3 = Adafruit 4-channel I2C-safe Bi-directional Logic Level Converter [part_number="Adafruit #757"]
  BeagleBone1 = BeagleBone Black
  Load_Cell1 = Load Cell - Red/white/black/green  # not connected
  Load_Cell2 = Load Cell - Red/white/black/green
  Load_Cell3 = Load Cell - Red/white/black/green
  Load_Cell4 = Load Cell - Red/white/black/green

nets:
  VCC: Part1.VCC, Part2.5V, Part3.B4
  GND: Part1.GND, Part2.GND, Part3.GND, BeagleBone1.no_name_yet#1
  N1: Part1.DO/RX, Part2.D6
  N2: Part1.CK/TX, Part2.D7
  N3: Part2.D1/TX, Part3.HV
  N4: Part2.D0/RX, Part3.B1
  N5: Part3.A4, BeagleBone1.no_name_yet#3, BeagleBone1.no_name_yet#5
  N6: Part3.A1, BeagleBone1.no_name_yet#20
  N7: Part3.LV, BeagleBone1.no_name_yet#19
  N8: Load_Cell2.wire1, Load_Cell3.wire1, Load_Cell4.wire1
  N9: Load_Cell2.wire2, Load_Cell3.wire2, Load_Cell4.wire2
  N10: Load_Cell2.wire3, Load_Cell3.wire3, Load_Cell4.wire3
  N11: Load_Cell2.wire4, Load_Cell3.wire4, Load_Cell4.wire4

custom parts:
  Adafruit 4-channel I2C-safe Bi-directional Logic Level Converter: Because the Arduino (and Basic Stamp) are 5V devices, and most modern sensors, displays, flash cards and modes are 3.3V-only, many makers find that they need to perform level shifting/conversion to protect the 3.3V device from 5V. We do have some other handy level shifters in the shop, from the DIP 74LVC245 to the fancy bi-directional TXB0108. However, neither of these are happy to work with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
  BeagleBone Black: BeagleBone Black rev. A5B
  Load Cell - Red/white/black/green: A rectangle load cell/weighting pressure Sensor with four wires - Red, white, black, green. Normally corresponding with E+, E-, A+, A- respectively.
