# Fritzing sketch breadboard (saved by Fritzing 0.9.3b)
breadboards: 1

parts:
  Part1 = Arduino Nano (Rev3.0)
  Part2 = HX711 Weighing Sensor Module
  Load_Cell1 = Load Cell - Red/white/black/green

nets:
  GND: Part1.GND, Part2.GND
  N1: Part1.D7, Part2.DO/RX
  N2: Part1.D8, Part2.CK/TX
  N3: Part2.E+, Load_Cell1.wire1
  N4: Part2.E-, Load_Cell1.wire3
  N5: Part2.A+, Load_Cell1.wire4
  N6: Part2.A-, Load_Cell1.wire2

custom parts:
  Load Cell - Red/white/black/green: A rectangle load cell/weighting pressure Sensor with four wires - Red, white, black, green. Normally corresponding with E+, E-, A+, A- respectively.
